// Logisim project labRISC.circ as structural Verilog: 8 circuits, main circuit main
module main (
);

  wire clock_1_out, cpu_1_illegal, cpu_1_load, cpu_1_store, or_1_out, rst_out;
  wire [31:0] cpu_1_memaddrs, cpu_1_pc, cpu_1_storevalue, memory_1_load_value, rom_1_data;

  Clock clock_1 (.out(clock_1_out));
  Button rst (.out(rst_out));
  or or_1 (or_1_out, cpu_1_illegal, clock_1_out);
  CPU cpu_1 (
    .Instruction(rom_1_data), .load_value(memory_1_load_value), .clk(or_1_out), .rst(rst_out),
    .illegal(cpu_1_illegal), .store(cpu_1_store), .load(cpu_1_load), .MemAddrs(cpu_1_memaddrs),
    .StoreValue(cpu_1_storevalue), .PC(cpu_1_pc));
  ROM #(.addrWidth(24), .dataWidth(32)) rom_1 (.addr(cpu_1_pc[25:2]), .data(rom_1_data));
  Memory memory_1 (
    .Address(cpu_1_memaddrs), .Store(cpu_1_store), .Load(cpu_1_load), .Store_Data(cpu_1_storevalue),
    .clk(or_1_out), .Load_Value(memory_1_load_value));

  // Notes on the sheet:
  //   contents of rom_1 (hex, n*v repeats v):
  //   413 51137 10113 22c00093 80e7 fea12823 fe812e23 40800413 ff014183 3401b3 1c183 ff114203 440233 24203
  //   4181b3 ff214203 440233 24203 4181b3 ff314203 440233 24203 4181b3 40000213 320233 24203 ffc12403
  //   420233 420233 410233 9400193 fe312823 9000193 fe312623 fec22203 20067 8067 ff410113 100513 112423
  //   22400093 80e7 ff010113 112623 12023 100793 6500693 12703 f70733 e12023 178793 fef12823 fed12623
  //   fe812e23 fe912c23 30000413 ff014183 340233 100193 320023 fec14183 3401b3 18023 24183 ff114483 940233
  //   100493 920023 fed14483 9404b3 48023 24483 9181b3 ff214483 940233 100493 920023 fee14483 9404b3 48023
  //   24483 9181b3 ff314483 940233 100493 920023 fef14483 9404b3 48023 24483 9181b3 40000213 320233 24203
  //   ff812483 ffc12403 420233 420233 410233 1a400193 fe312823 bc00193 fe312623 fec22203 20067 12503
  //   fffff7b7 c4678793 f50533 fea12823 fe812e23 40800413 ff014183 3401b3 1c183 ff114203 440233 24203
  //   4181b3 ff214203 440233 24203 4181b3 ff314203 440233 24203 4181b3 40000213 320233 24503 ffc12403
  //   1400093 80e7 c12083 513 1010113 8067 22400213 20067 ff410113 48537 60050513 112423 a800093 80e7
  //   22400093 80e7 109*0 1 0 1010100 63*1010101 100 1000101 1010100 1000000 1010100 121*0 64*1000100
  //   64*2020000 64*3020100 0 4040404 0 4040404 0 4040404 0 4040404 0 4040404 0 4040404 0 4040404 0
  //   4040404 0 4040404 0 4040404 0 4040404 0 4040404 0 4040404 0 4040404 0 4040404 0 4040404 0 4040404 0
  //   4040404 0 4040404 0 4040404 0 4040404 0 4040404 0 4040404 0 4040404 0 4040404 0 4040404 0 4040404 0
  //   4040404 0 4040404 0 4040404 0 4040404 0 4040404 1000100 5040504 1000100 5040504 1000100 5040504
  //   1000100 5040504 1000100 5040504 1000100 5040504 1000100 5040504 1000100 5040504 1000100 5040504
  //   1000100 5040504 1000100 5040504 1000100 5040504 1000100 5040504 1000100 5040504 1000100 5040504
  //   1000100 5040504 1000100 5040504 1000100 5040504 1000100 5040504 1000100 5040504 1000100 5040504
  //   1000100 5040504 1000100 5040504 1000100 5040504 1000100 5040504 1000100 5040504 1000100 5040504
  //   1000100 5040504 1000100 5040504 1000100 5040504 1000100 5040504 1000100 5040504 2020000 6060404
  //   2020000 6060404 2020000 6060404 2020000 6060404 2020000 6060404 2020000 6060404 2020000 6060404
  //   2020000 6060404 2020000 6060404 2020000 6060404 2020000 6060404 2020000 6060404 2020000 6060404
  //   2020000 6060404 2020000 6060404 2020000 6060404 2020000 6060404 2020000 6060404 2020000 6060404
  //   2020000 6060404 2020000 6060404 2020000 6060404 2020000 6060404 2020000 6060404 2020000 6060404
  //   2020000 6060404 2020000 6060404 2020000 6060404 2020000 6060404 2020000 6060404 2020000 6060404
  //   2020000 6060404 3020100 7060504 3020100 7060504 3020100 7060504 3020100 7060504 3020100 7060504
  //   3020100 7060504 3020100 7060504 3020100 7060504 3020100 7060504 3020100 7060504 3020100 7060504
  //   3020100 7060504 3020100 7060504 3020100 7060504 3020100 7060504 3020100 7060504 3020100 7060504
  //   3020100 7060504 3020100 7060504 3020100 7060504 3020100 7060504 3020100 7060504 3020100 7060504
  //   3020100 7060504 3020100 7060504 3020100 7060504 3020100 7060504 3020100 7060504 3020100 7060504
  //   3020100 7060504 3020100 7060504 3020100 7060504 0 0 8080808 8080808 0 0 8080808 8080808 0 0 8080808
  //   8080808 0 0 8080808 8080808 0 0 8080808 8080808 0 0 8080808 8080808 0 0 8080808 8080808 0 0 8080808
  //   8080808 0 0 8080808 8080808 0 0 8080808 8080808 0 0 8080808 8080808 0 0 8080808 8080808 0 0 8080808
  //   8080808 0 0 8080808 8080808 0 0 8080808 8080808 0 0 8080808 8080808 1000100 1000100 9080908 9080908
  //   1000100 1000100 9080908 9080908 1000100 1000100 9080908 9080908 1000100 1000100 9080908 9080908
  //   1000100 1000100 9080908 9080908 1000100 1000100 9080908 9080908 1000100 1000100 9080908 9080908
  //   1000100 1000100 9080908 9080908 1000100 1000100 9080908 9080908 1000100 1000100 9080908 9080908
  //   1000100 1000100 9080908 9080908 1000100 1000100 9080908 9080908 1000100 1000100 9080908 9080908
  //   1000100 1000100 9080908 9080908 1000100 1000100 9080908 9080908 1000100 1000100 9080908 9080908
  //   2020000 2020000 a0a0808 a0a0808 2020000 2020000 a0a0808 a0a0808 2020000 2020000 a0a0808 a0a0808
  //   2020000 2020000 a0a080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
endmodule

module extractor (
  input  [31:0] inst_in,
  input  [2:0] foramt,
  output [6:0] opcode,
  output [4:0] Rd,
  output [2:0] func3,
  output [4:0] Rs1,
  output [4:0] Rs2,
  output bit30,
  output [31:0] imm_out
);

  Multiplexer #(.select(3), .width(32)) multiplexer_1 (
    .in1({{21{inst_in[31]}}, inst_in[30:20]}), .in2({{21{inst_in[31]}}, inst_in[30:25], inst_in[11:7]}),
    .in3({{20{inst_in[31]}}, inst_in[30], inst_in[7], inst_in[29:25], inst_in[11:8], 1'b0}),
    .in4({inst_in[31:12], {12{1'b0}}}),
    .in5({{12{inst_in[31]}}, inst_in[19:12], inst_in[30], inst_in[20], inst_in[29:21], 1'b0}),
    .in6({32{1'b0}}), .in7({32{1'b0}}), .out(imm_out), .sel(foramt));  // open: in0

  assign bit30 = inst_in[30];
  assign func3 = inst_in[14:12];
  assign opcode = inst_in[6:0];
  assign Rd = inst_in[11:7];
  assign Rs1 = inst_in[19:15];
  assign Rs2 = inst_in[24:20];

  // Notes on the sheet:
  //   I type
  //   S type
  //   B type
  //   U type
  //   J type
endmodule

module ALU (
  input  [31:0] A,
  input  [31:0] B,
  input  [2:0] Fun3,
  input  bit30,
  input  imm,
  output [31:0] Data
);

  wire and_1_out, not_1_out;
  wire [0:0] comparator_1_lt, comparator_2_lt;
  wire [31:0] adder_1_out, and_2_out, multiplexer_1_out, multiplexer_2_out, or_1_out, shifter_1_out,
       shifter_2_out, shifter_3_out, subtractor_1_out, xor_1_out;

  Adder #(.width(32)) adder_1 (.a(A), .b(B), .out(adder_1_out));  // open: cin, cout
  Subtractor #(.width(32)) subtractor_1 (.a(A), .b(B), .out(subtractor_1_out));  // open: bin, bout
  and and_1 (and_1_out, bit30, not_1_out);
  not not_1 (not_1_out, imm);
  Comparator #(.width(32)) comparator_1 (.a(A), .b(B), .lt(comparator_1_lt[0]));  // open: gt, eq
  Comparator #(.mode("unsigned"), .width(32)) comparator_2 (.a(A), .b(B), .lt(comparator_2_lt[0]));  // open: gt, eq
  assign xor_1_out = A ^ B;  // XOR_Gate xor_1, 32 bits wide
  assign or_1_out = A | B;  // OR_Gate or_1, 32 bits wide
  assign and_2_out = A & B;  // AND_Gate and_2, 32 bits wide
  Shifter #(.width(32)) shifter_1 (.in(A), .\dist (B[4:0]), .out(shifter_1_out));
  Shifter #(.shift("lr"), .width(32)) shifter_2 (.in(A), .\dist (B[4:0]), .out(shifter_2_out));
  Shifter #(.shift("ar"), .width(32)) shifter_3 (.in(A), .\dist (B[4:0]), .out(shifter_3_out));
  Multiplexer #(.width(32)) multiplexer_1 (
    .in0(adder_1_out), .in1(subtractor_1_out), .out(multiplexer_1_out), .sel(and_1_out));
  Multiplexer #(.width(32)) multiplexer_2 (
    .in0(shifter_2_out), .in1(shifter_3_out), .out(multiplexer_2_out), .sel(bit30));
  Multiplexer #(.select(3), .width(32)) multiplexer_3 (
    .in0(multiplexer_1_out), .in1({{31{1'b0}}, comparator_1_lt[0]}), .in2({{31{1'b0}}, comparator_2_lt[0]}),
    .in3(xor_1_out), .in4(or_1_out), .in5(and_2_out), .in6(shifter_1_out), .in7(multiplexer_2_out),
    .out(Data), .sel(Fun3));
endmodule

module GPR (
  input  [31:0] wdata,
  input  [3:0] Rd,
  input  Write,
  input  [3:0] Rs1,
  input  [3:0] Rs2,
  input  clk,
  output [31:0] out1,
  output [31:0] out2
);

  wire decoder_1_out1, decoder_1_out2, decoder_1_out3, decoder_1_out4, decoder_1_out5, decoder_1_out6,
       decoder_1_out7, decoder_1_out8, decoder_1_out9, decoder_1_out10, decoder_1_out11, decoder_1_out12,
       decoder_1_out13, decoder_1_out14, decoder_1_out15;
  wire [31:0] register_1_q, register_2_q, register_3_q, register_4_q, register_5_q, register_6_q,
       register_7_q, register_8_q, register_9_q, register_10_q, register_11_q, register_12_q, register_13_q,
       register_14_q, register_15_q;

  Decoder #(.select(4)) decoder_1 (
    .out1(decoder_1_out1), .out2(decoder_1_out2), .out3(decoder_1_out3), .out4(decoder_1_out4),
    .out5(decoder_1_out5), .out6(decoder_1_out6), .out7(decoder_1_out7), .out8(decoder_1_out8),
    .out9(decoder_1_out9), .out10(decoder_1_out10), .out11(decoder_1_out11), .out12(decoder_1_out12),
    .out13(decoder_1_out13), .out14(decoder_1_out14), .out15(decoder_1_out15), .sel(Rd), .en(Write));  // open: out0
  Register #(.trigger("falling"), .width(32)) register_1 (
    .D(wdata), .en(decoder_1_out8), .clk(clk), .Q(register_1_q));  // open: clr
  Register #(.trigger("falling"), .width(32)) register_2 (
    .D(wdata), .en(decoder_1_out1), .clk(clk), .Q(register_2_q));  // open: clr
  Register #(.trigger("falling"), .width(32)) register_3 (
    .D(wdata), .en(decoder_1_out9), .clk(clk), .Q(register_3_q));  // open: clr
  Register #(.trigger("falling"), .width(32)) register_4 (
    .D(wdata), .en(decoder_1_out2), .clk(clk), .Q(register_4_q));  // open: clr
  Register #(.trigger("falling"), .width(32)) register_5 (
    .D(wdata), .en(decoder_1_out10), .clk(clk), .Q(register_5_q));  // open: clr
  Register #(.trigger("falling"), .width(32)) register_6 (
    .D(wdata), .en(decoder_1_out3), .clk(clk), .Q(register_6_q));  // open: clr
  Register #(.trigger("falling"), .width(32)) register_7 (
    .D(wdata), .en(decoder_1_out11), .clk(clk), .Q(register_7_q));  // open: clr
  Register #(.trigger("falling"), .width(32)) register_8 (
    .D(wdata), .en(decoder_1_out4), .clk(clk), .Q(register_8_q));  // open: clr
  Register #(.trigger("falling"), .width(32)) register_9 (
    .D(wdata), .en(decoder_1_out12), .clk(clk), .Q(register_9_q));  // open: clr
  Register #(.trigger("falling"), .width(32)) register_10 (
    .D(wdata), .en(decoder_1_out5), .clk(clk), .Q(register_10_q));  // open: clr
  Register #(.trigger("falling"), .width(32)) register_11 (
    .D(wdata), .en(decoder_1_out13), .clk(clk), .Q(register_11_q));  // open: clr
  Register #(.trigger("falling"), .width(32)) register_12 (
    .D(wdata), .en(decoder_1_out6), .clk(clk), .Q(register_12_q));  // open: clr
  Register #(.trigger("falling"), .width(32)) register_13 (
    .D(wdata), .en(decoder_1_out14), .clk(clk), .Q(register_13_q));  // open: clr
  Register #(.trigger("falling"), .width(32)) register_14 (
    .D(wdata), .en(decoder_1_out7), .clk(clk), .Q(register_14_q));  // open: clr
  Register #(.trigger("falling"), .width(32)) register_15 (
    .D(wdata), .en(decoder_1_out15), .clk(clk), .Q(register_15_q));  // open: clr
  Multiplexer #(.select(4), .width(32)) multiplexer_1 (
    .in0({32{1'b0}}), .in1(register_2_q), .in2(register_4_q), .in3(register_6_q), .in4(register_8_q),
    .in5(register_10_q), .in6(register_12_q), .in7(register_14_q), .in8(register_1_q), .in9(register_3_q),
    .in10(register_5_q), .in11(register_7_q), .in12(register_9_q), .in13(register_11_q),
    .in14(register_13_q), .in15(register_15_q), .out(out1), .sel(Rs1));
  Multiplexer #(.select(4), .width(32)) multiplexer_2 (
    .in0({32{1'b0}}), .in1(register_2_q), .in2(register_4_q), .in3(register_6_q), .in4(register_8_q),
    .in5(register_10_q), .in6(register_12_q), .in7(register_14_q), .in8(register_1_q), .in9(register_3_q),
    .in10(register_5_q), .in11(register_7_q), .in12(register_9_q), .in13(register_11_q),
    .in14(register_13_q), .in15(register_15_q), .out(out2), .sel(Rs2));
endmodule

module Register_File (
  input  [31:0] Data,
  input  [4:0] Rd,
  input  Write,
  input  [4:0] Rs1,
  input  [4:0] Rs2,
  input  clk,
  output [31:0] out1,
  output [31:0] out2
);

  GPR gpr_1 (
    .wdata(Data), .Rd(Rd[3:0]), .Write(Write), .Rs1(Rs1[3:0]), .Rs2(Rs2[3:0]), .clk(clk), .out1(out1),
    .out2(out2));
endmodule

module BranchUnit (
  input  [31:0] A,
  input  [31:0] B,
  input  [2:0] fun3,
  output Branch
);

  wire comparator_1_eq, comparator_1_gt, comparator_1_lt, comparator_2_eq, comparator_2_gt, comparator_2_lt,
       not_1_out, or_1_out, or_2_out;

  Comparator #(.width(32)) comparator_1 (
    .a(A), .b(B), .gt(comparator_1_gt), .eq(comparator_1_eq), .lt(comparator_1_lt));
  Comparator #(.mode("unsigned"), .width(32)) comparator_2 (
    .a(A), .b(B), .gt(comparator_2_gt), .eq(comparator_2_eq), .lt(comparator_2_lt));
  or or_1 (or_1_out, comparator_1_gt, comparator_1_eq);
  or or_2 (or_2_out, comparator_2_gt, comparator_2_eq);
  not not_1 (not_1_out, comparator_1_eq);
  Multiplexer #(.select(3)) multiplexer_1 (
    .in0(comparator_1_eq), .in1(not_1_out), .in2(comparator_1_lt), .in3(or_1_out), .in4(comparator_2_lt),
    .in5(or_2_out), .in6(1'b0), .in7(1'b0), .out(Branch), .sel(fun3));
endmodule

module Memory (
  input  [31:0] Address,
  input  Store,
  input  Load,
  input  [31:0] Store_Data,
  input  clk,
  output [31:0] Load_Value
);

  RAM #(.addrWidth(24), .asyncread("true"), .dataWidth(32), .trigger("falling")) Memory (
    .addr(Address[25:2]), .we(Store), .oe(Load), .clk(clk), .din(Store_Data), .dout(Load_Value));
endmodule

module CPU (
  input  [31:0] Instruction,
  input  [31:0] load_value,
  input  clk,
  input  rst,
  output illegal,
  output store,
  output load,
  output [31:0] MemAddrs,
  output [31:0] StoreValue,
  output [31:0] PC
);

  wire and_1_out, branchunit_1_branch, decoder_1_out1, decoder_1_out2, decoder_1_out3, decoder_1_out4,
       decoder_1_out5, decoder_1_out6, decoder_1_out7, decoder_1_out9, decoder_1_out10, decoder_1_out11,
       decoder_1_out12, decoder_1_out13, decoder_1_out14, decoder_1_out15, decoder_1_out16, decoder_1_out17,
       decoder_1_out18, decoder_1_out19, decoder_1_out20, decoder_1_out21, decoder_1_out22, decoder_1_out23,
       decoder_1_out24, decoder_1_out25, decoder_1_out26, decoder_1_out27, decoder_1_out28, decoder_1_out29,
       decoder_1_out30, decoder_1_out31, extractor_1_bit30, nand_1_out, or_2_out, or_4_out, or_5_out,
       or_6_out, or_7_out, priority_encoder_1_p2;
  wire [1:0] extractor_1_opcode;
  wire [2:0] extractor_1_func3, priority_encoder_1_p5;
  wire [4:0] extractor_1_opcode_2, extractor_1_rd, extractor_1_rs1, extractor_1_rs2;
  wire [31:0] adder_1_out, adder_2_out, adder_3_out, adder_4_out, alu_1_data, controlled_buffer_1_out,
       extractor_1_imm_out, multiplexer_1_out, multiplexer_3_out, register_file_1_out1, register_file_1_out2;

  Decoder #(.select(5)) decoder_1 (
    .out0(load), .out1(decoder_1_out1), .out2(decoder_1_out2), .out3(decoder_1_out3), .out4(decoder_1_out4),
    .out5(decoder_1_out5), .out6(decoder_1_out6), .out7(decoder_1_out7), .out8(store), .out9(decoder_1_out9),
    .out10(decoder_1_out10), .out11(decoder_1_out11), .out12(decoder_1_out12), .out13(decoder_1_out13),
    .out14(decoder_1_out14), .out15(decoder_1_out15), .out16(decoder_1_out16), .out17(decoder_1_out17),
    .out18(decoder_1_out18), .out19(decoder_1_out19), .out20(decoder_1_out20), .out21(decoder_1_out21),
    .out22(decoder_1_out22), .out23(decoder_1_out23), .out24(decoder_1_out24), .out25(decoder_1_out25),
    .out26(decoder_1_out26), .out27(decoder_1_out27), .out28(decoder_1_out28), .out29(decoder_1_out29),
    .out30(decoder_1_out30), .out31(decoder_1_out31), .sel(extractor_1_opcode_2));  // open: en
  nand nand_1 (nand_1_out, extractor_1_opcode[1], extractor_1_opcode[0]);
  extractor extractor_1 (
    .inst_in(Instruction), .foramt(priority_encoder_1_p5),
    .opcode({extractor_1_opcode_2, extractor_1_opcode}), .Rd(extractor_1_rd), .func3(extractor_1_func3),
    .Rs1(extractor_1_rs1), .Rs2(extractor_1_rs2), .bit30(extractor_1_bit30), .imm_out(extractor_1_imm_out));
  or or_1 (illegal, nand_1_out, decoder_1_out31, decoder_1_out30, decoder_1_out29, decoder_1_out26, decoder_1_out23, decoder_1_out22, decoder_1_out21, decoder_1_out20, decoder_1_out19, decoder_1_out18, decoder_1_out28, decoder_1_out17, decoder_1_out16, decoder_1_out15, decoder_1_out14, decoder_1_out11, decoder_1_out10, decoder_1_out9, decoder_1_out7, decoder_1_out6, decoder_1_out2, decoder_1_out1);
  assign controlled_buffer_1_out = decoder_1_out5 ? adder_1_out : 32'bz;  // Controlled_Buffer controlled_buffer_1
  Adder #(.width(32)) adder_1 (.a(PC), .b(extractor_1_imm_out), .out(adder_1_out));  // open: cin, cout
  Multiplexer #(.width(32)) multiplexer_1 (
    .in0(adder_3_out), .in1(adder_2_out), .out(multiplexer_1_out), .sel(decoder_1_out25));
  Register #(.trigger("falling"), .width(32)) register_1 (
    .D(multiplexer_1_out), .clk(clk), .Q(PC), .clr(rst));  // open: en
  Adder #(.width(32)) adder_2 (
    .a(register_file_1_out1), .b(extractor_1_imm_out), .out(adder_2_out));  // open: cin, cout
  Adder #(.width(32)) adder_3 (.a(PC), .b(multiplexer_3_out), .out(adder_3_out));  // open: cin, cout
  Adder #(.width(32)) adder_4 (.a(PC), .b(32'h4), .out(adder_4_out));  // open: cin, cout
  or or_2 (or_2_out, decoder_1_out13, decoder_1_out5);
  // Priority_Encoder priority_encoder_1: pin names not known; wires that end beside it: decoder_1_out12, priority_encoder_1_p2, store, decoder_1_out24, priority_encoder_1_p5, or_2_out, decoder_1_out27, 1'b0, 1'b0
  Register_File register_file_1 (
    .Data(controlled_buffer_1_out), .Rd(extractor_1_rd), .Write(or_6_out), .Rs1(extractor_1_rs1),
    .Rs2(extractor_1_rs2), .clk(clk), .out1(register_file_1_out1), .out2(register_file_1_out2));
  assign controlled_buffer_1_out = or_5_out ? adder_4_out : 32'bz;  // Controlled_Buffer controlled_buffer_2
  or or_3 (priority_encoder_1_p2, decoder_1_out28, decoder_1_out25, decoder_1_out4, decoder_1_out3, load);
  Multiplexer #(.width(32)) multiplexer_2 (
    .in0(register_file_1_out2), .in1(extractor_1_imm_out), .out(StoreValue), .sel(decoder_1_out4));
  assign controlled_buffer_1_out = decoder_1_out13 ? extractor_1_imm_out : 32'bz;  // Controlled_Buffer controlled_buffer_3
  Multiplexer #(.width(32)) multiplexer_3 (
    .in0(32'h4), .in1(extractor_1_imm_out), .out(multiplexer_3_out), .sel(or_4_out));
  or or_4 (or_4_out, and_1_out, decoder_1_out27);
  or or_5 (or_5_out, decoder_1_out27, decoder_1_out25);
  or or_6 (or_6_out, decoder_1_out27, decoder_1_out25, decoder_1_out5, load, decoder_1_out4, decoder_1_out12, decoder_1_out13);
  and and_1 (and_1_out, branchunit_1_branch, decoder_1_out24);
  or or_7 (or_7_out, decoder_1_out12, decoder_1_out4);
  ALU alu_1 (
    .A(register_file_1_out1), .B(StoreValue), .Fun3(extractor_1_func3), .bit30(extractor_1_bit30),
    .imm(decoder_1_out4), .Data(alu_1_data));
  assign controlled_buffer_1_out = or_7_out ? alu_1_data : 32'bz;  // Controlled_Buffer controlled_buffer_4
  BranchUnit branchunit_1 (
    .A(register_file_1_out1), .B(StoreValue), .fun3(extractor_1_func3), .Branch(branchunit_1_branch));
  assign controlled_buffer_1_out = load ? load_value : 32'bz;  // Controlled_Buffer controlled_buffer_5
  Adder #(.width(32)) adder_5 (.a(register_file_1_out1), .b(extractor_1_imm_out), .out(MemAddrs));  // open: cin, cout
endmodule
